# Fritzing sketch Circuit (saved by Fritzing 0.9.3b)
breadboards: 1

parts:
  Part1 = Adafruit Trinket M0 [part_number="Adafruit #3500"]
  GY1 = MPU-6050 Board GY-521 [form="♀ (female)" package=THT]
  J1 = Piezo Speaker

nets:
  N1: Part1.GND, GY1.pin2, J1.pin1
  N2: Part1.D4_A2_PA06_TXD_MOSI, J1.pin2
  N3: Part1.3.3V, GY1.pin1
  N4: Part1.D2_A1_PA09_SCL_MISO, GY1.pin3
  N5: Part1.D0_A4_PA08_SDA, GY1.pin4

custom parts:
  MPU-6050 Board GY-521: Acelerometro y Giroscopio MPU-6050 Board GY-521
